# Fritzing sketch Cableado erronka 10 (1) (saved by Fritzing 0.9.3b)
breadboards: 1

parts:
  Componente1 = iceZUM Alhambra
  CNY70-1 = CNY70 [package=cny70-side]
  CNY70-2 = CNY70 [package=cny70-side]
  CNY70-3 = CNY70 [package=cny70-side]
  CNY70-4 = CNY70 [package=cny70-side]
  R1 = Resistor [tolerance=±5% resistance=330 package="2512 [SMD]"]
  R8 = Resistor [tolerance=±5% resistance=56k package="2512 [SMD]"]
  U1 = LIPO-2000mAh [package=lipo-2000]
  U2 = LM2596 step down module
  M2 = DC Motor
  D1 = Diode [package=diode-1n4001]
  D2 = Diode [package=diode-1n4001]  # not connected
  R9 = Resistor [tolerance=±5% resistance=330 package="2512 [SMD]"]
  R10 = Resistor [tolerance=±5% resistance=330 package="2512 [SMD]"]
  R11 = Resistor [tolerance=±5% resistance=330 package="2512 [SMD]"]
  R12 = Resistor [tolerance=±5% resistance=56k package="2512 [SMD]"]
  R13 = Resistor [tolerance=±5% resistance=56k package="2512 [SMD]"]
  R14 = Resistor [tolerance=±5% resistance=56k package="2512 [SMD]"]
  Componente2 = Motor Driver 1A Dual TB6612FNG
  M3 = DC Motor

nets:
  N1: Componente1.D3, Componente1.V3, CNY70-4.E, R8.Pin_0
  N2: Componente1.D4, Componente1.V4, CNY70-3.E, R12.Pin_0
  N3: Componente1.D5, CNY70-2.E, R14.Pin_0
  N4: Componente1.D6, Componente1.V6, CNY70-1.E, R13.Pin_0
  N5: Componente1.D7, Componente1.V7, Componente2.PWMB
  N6: Componente1.D8, Componente1.V8, Componente2.BIN2
  N7: Componente1.D9, Componente2.BIN1
  N8: Componente1.D10, Componente2.STBY
  N9: Componente1.D11, Componente2.AIN1
  N10: Componente1.D12, Componente2.AIN2
  N11: Componente1.D13, Componente2.PWMA
  N12: Componente1.G0, Componente1.GA2, R1.Pin_1, R8.Pin_1, U1.-, U2.IN-, U2.OUT-, R9.Pin_1, R10.Pin_1, R11.Pin_1, R12.Pin_1, R13.Pin_1, R14.Pin_1, Componente2.GND
  N13: Componente1.5VP, CNY70-1.A, CNY70-1.C, CNY70-2.A, CNY70-2.C, CNY70-3.A, CNY70-3.C, CNY70-4.A, CNY70-4.C, Componente2.VCC
  N14: CNY70-1.K, R11.Pin_0
  N15: CNY70-2.K, R10.Pin_0
  N16: CNY70-3.K, R9.Pin_0
  N17: CNY70-4.K, R1.Pin_0
  N18: U1.+, U2.IN+, D1.A
  N19: M2.pin_1, Componente2.B02
  N20: M2.pin_2, Componente2.B01
  N21: Componente2.A02, M3.pin_1
  N22: Componente2.A01, M3.pin_2

notes:
  7V

custom parts:
  iceZUM Alhambra: Arduino/zum compatible Open FPGA electronic board. Synthesize hardware easily, using only open source tools
  CNY70: PHOTOTRANSISTOR
  LM2596 step down module: LM2596 DC-DC step down power supply module 3 A.
